# Fritzing sketch simon (saved by Fritzing 0.8.7b)
breadboards: 1

parts:
  Parte1 = Arduino Leonardo (Rev3b)
  S1 = Pushbutton [package="[THT]"]
  S2 = Pushbutton [package="[THT]"]
  S3 = Pushbutton [package="[THT]"]
  S4 = Pushbutton [package="[THT]"]
  R1 = Resistor [tolerance=±5% resistance=220 package=THT]
  R2 = Resistor [tolerance=±5% resistance=220 package=THT]
  R3 = Resistor [tolerance=±5% resistance=220 package=THT]
  R4 = Resistor [tolerance=±5% resistance=220 package=THT]
  LED1 = LED - 3mm [color="Red (633nm)" package="3 mm [THT]"]
  LED3 = LED - 3mm [color="Yellow (595nm)" package="3 mm [THT]"]
  LED4 = LED - 3mm [color="Blue (525nm)" package="3 mm [THT]"]
  LED5 = LED - 3mm [color="Green (565nm)" package="3 mm [THT]"]
  R5 = Resistor [tolerance=±5% resistance=220 package=THT]
  R6 = Resistor [tolerance=±5% resistance=220 package=THT]
  R7 = Resistor [tolerance=±5% resistance=220 package=THT]
  R8 = Resistor [tolerance=±5% resistance=220 package=THT]
  J1 = Piezo Speaker

nets:
  N1: Parte1.D0/RX, S1.Pin_1, S1.Pin_2, R1.Pin_0
  N2: Parte1.D1/TX, LED1.anode
  N3: Parte1.D2/SDA, Parte1.SDA, S2.Pin_3, S2.Pin_4, R2.Pin_0
  N4: Parte1.D3_PWM/SCL, LED5.anode
  N5: Parte1.D4/A6, S3.Pin_3, S3.Pin_4, R3.Pin_0
  N6: Parte1.D5_PWM, LED3.anode
  N7: Parte1.D6_PWM/A7, S4.Pin_3, S4.Pin_4, R4.Pin_0
  N8: Parte1.D7, LED4.anode
  N9: Parte1.5V, S1.Pin_3, S1.Pin_4, S2.Pin_1, S2.Pin_2, S3.Pin_1, S3.Pin_2, S4.Pin_1, S4.Pin_2
  N10: Parte1.GND, R1.Pin_1, R2.Pin_1, R3.Pin_1, R4.Pin_1, R5.Pin_1, R6.Pin_1, R7.Pin_1, R8.Pin_1, J1.pin1
  N11: Parte1.D9_PWM/A9, J1.pin2
  N12: LED1.cathode, R5.Pin_0
  N13: LED3.cathode, R7.Pin_0
  N14: LED4.cathode, R8.Pin_0
  N15: LED5.cathode, R6.Pin_0
